# Fritzing sketch Project 1 Fritzing (saved by Fritzing 0.9.3b)
breadboards: 3

parts:
  Part1 = Arduino Uno (Rev3)  # not connected
  Part2 = 2A MOTOR SHIELD 9
  hc-sr1 = hc-sr04
  T1 = LM35 Temperature Sensor [package="TO92 [THT]"]
  J1 = Basic Servo
  M2 = DC Motor  # not connected
  M3 = DC Motor  # not connected
  3-pins_Hall_Effect_Sensor1 = mystery part, 3 pins [chip_label="Hall Effect Sensor"]
  3-pins_Hall_Effect_Sensor2 = mystery part, 3 pins [chip_label="Hall Effect Sensor"]
  LCD1 = LCD screen
  U1 = POT [package=pot_alpha_rv16af-20]
  Q1 = PHOTOTRANSISTOR REFLECTIVE OBJECT SENSOR [package=qrb1114-side]
  Q2 = PHOTOTRANSISTOR REFLECTIVE OBJECT SENSOR [package=qrb1114-side]
  R3 = Resistor [tolerance=±5% resistance=220 package="2512 [SMD]"]
  R4 = Resistor [tolerance=±5% resistance=220 package="2512 [SMD]"]
  R5 = Resistor [tolerance=±5% resistance=220 package="2512 [SMD]"]
  R6 = Resistor [tolerance=±5% resistance=220 package="2512 [SMD]"]
  BT1 = Bluetooth HC-06u [package=THT]
  SW1 = DIP SWITCH [package=dipswitch-02]
  R7 = Resistor [tolerance=±5% resistance=10k package="0603 [SMD]"]
  R8 = Resistor [tolerance=±5% resistance=10k package="0603 [SMD]"]
  U2 = 74HC595 [package="DIP16 [THT]"]
  R9 = Resistor [tolerance=±5% resistance=10k package="0603 [SMD]"]

nets:
  N1: Part2.D3, 3-pins_Hall_Effect_Sensor1.pin1
  N2: Part2.D11, U2.DS
  N3: Part2.A4, SW1.1, R7.Pin_0
  N4: Part2.A1, J1.pulse
  N5: Part2.D13, hc-sr1.Trig
  VCC: Part2.5V, hc-sr1.VCC, T1.Vout, J1.vcc, 3-pins_Hall_Effect_Sensor1.pin3, 3-pins_Hall_Effect_Sensor2.pin3, LCD1.VDD, U1.S, Q1.A, Q2.A, R3.Pin_0, R5.Pin_0, BT1.VCC, SW1.3, SW1.4, U2.MR, U2.VCC, R9.Pin_1
  N6: Part2.A2, Q1.C, R3.Pin_1
  N7: Part2.D2, 3-pins_Hall_Effect_Sensor2.pin1
  N8: Part2.D10, U2.ST_CP
  N9: Part2.A5, SW1.2, R8.Pin_0
  N10: Part2.A0, T1.+Vs
  N11: Part2.D12, hc-sr1.Echo
  GND: Part2.GND, hc-sr1.GND, T1.GND, J1.gnd, 3-pins_Hall_Effect_Sensor1.pin2, 3-pins_Hall_Effect_Sensor2.pin2, LCD1.VSS, LCD1.R/W, LCD1.LED-, U1.E, Q1.E, Q2.E, R4.Pin_0, R6.Pin_0, BT1.GND, R7.Pin_1, R8.Pin_1, U2.GND, U2.OE
  N12: Part2.A3, Q2.C, R5.Pin_1
  N13: Part2.D1, BT1.TXD
  N14: Part2.D9, U2.SH_CP
  N15: LCD1.V0, U1.A
  N16: LCD1.RS, U2.Q4
  N17: LCD1.E, U2.Q5
  N18: LCD1.DB4, U2.Q0
  N19: LCD1.DB5, U2.Q1
  N20: LCD1.DB6, U2.Q2
  N21: LCD1.DB7, U2.Q3
  N22: LCD1.LED+, R9.Pin_0
  N23: Q1.K, R4.Pin_1
  N24: Q2.K, R6.Pin_1

custom parts:
  Bluetooth HC-06u: Bluetooth HC-06 - face up, pins down 16.5mm x 37.5mm PCB
